# Fritzing sketch buttons-leds (saved by Fritzing 0.8.0b)
breadboards: 1

parts:
  LED1 = LED - 5mm [color="Red (633nm)" package="5 mm [THT]"]
  R1 = Resistor [tolerance=±5% resistance=220 package=THT]
  Part1 = Arduino Leonardo (Rev3b)
  R2 = Resistor [tolerance=±5% resistance=220 package=THT]
  LED2 = LED - 5mm [color="Red (633nm)" package="5 mm [THT]"]
  S1 = Pushbutton [package="[THT]"]
  R3 = Resistor [tolerance=±5% resistance=220 package=THT]
  LED3 = LED - 5mm [color="Red (633nm)" package="5 mm [THT]"]
  R4 = Resistor [tolerance=±5% resistance=220 package=THT]
  S2 = Pushbutton [package="[THT]"]

nets:
  N1: LED1.cathode, R1.Pin_1
  N2: R1.Pin_0, Part1.GND, R2.Pin_0, S1.Pin_3, S1.Pin_4, R4.Pin_0
  N3: Part1.D5_PWM, S1.Pin_1, S1.Pin_2, R3.Pin_1
  N4: Part1.5V, S2.Pin_1, S2.Pin_2
  N5: Part1.D11_PWM, LED2.anode
  N6: R2.Pin_1, LED2.cathode
  N7: LED3.cathode, R4.Pin_1
  N8: LED3.anode, S2.Pin_3, S2.Pin_4
