# Fritzing sketch example_circuits (saved by Fritzing 0.8.5b)
breadboards: 1

parts:
  R1 = Rotary Potentiometer (Small) [maximum_resistance=100kΩ package=THT]
  S1 = Pushbutton [package="[THT]"]
  R2 = Resistor [tolerance=±5% resistance=220 package=THT]
  S2 = Pushbutton [package="[THT]"]
  R3 = Resistor [tolerance=±5% resistance=220 package=THT]
  LED1 = LED - 5mm [color="Red (633nm)" package="5 mm [THT]"]
  R4 = Resistor [tolerance=±5% resistance=220 package=THT]
  R5 = Photocell (LDR) [package=THT]
  R6 = Resistor [tolerance=±5% resistance=220 package=THT]
  MIC1 = Microphone
  J1 = Basic Servo

nets:
  N1: R1.leg1, S1.Pin_1, S1.Pin_2, R3.Pin_1, MIC1.pin1, J1.gnd
  N2: R1.leg2, J1.vcc, J1.pulse
  N3: S1.Pin_3, S1.Pin_4, R2.Pin_1
  N4: R2.Pin_0, S2.Pin_3, S2.Pin_4, R5.pin_1
  N5: S2.Pin_1, S2.Pin_2, R3.Pin_0
  N6: LED1.cathode, R4.Pin_1
  N7: R4.Pin_0, R6.Pin_0
  N8: R5.pin_0, R6.Pin_1
