# Fritzing sketch potentiometers-servos (saved by Fritzing 0.8.5b)
breadboards: 1

parts:
  R1 = Rotary Potentiometer (Small) [maximum_resistance=100kΩ package=THT]
  R2 = Rotary Potentiometer (Small) [maximum_resistance=100kΩ package=THT]
  R3 = Resistor [tolerance=±5% resistance=220 package=THT]
  LED1 = LED - 5mm [color="Red (633nm)" package="5 mm [THT]"]
  J1 = Basic Servo
  Part1 = Arduino Leonardo (Rev3b)

nets:
  GND: R1.leg1, R2.leg1, R3.Pin_0, J1.gnd, Part1.GND
  N1: R1.wiper, Part1.A0
  VCC: R1.leg2, R2.leg2, J1.vcc, Part1.5V
  N2: R2.wiper, Part1.A1
  N3: R3.Pin_1, LED1.cathode
  N4: LED1.anode, Part1.D3_PWM/SCL
  N5: J1.pulse, Part1.D13_PWM
