# Fritzing sketch pull-up-down (saved by Fritzing 0.8.0b)
breadboards: 1

parts:
  S1 = Pushbutton [package="[THT]"]
  R3 = Resistor [tolerance=±5% resistance=220 package=THT]
  Part1 = Arduino Leonardo (Rev3b)
  S2 = Pushbutton [package="[THT]"]
  R4 = Resistor [tolerance=±5% resistance=220 package=THT]

nets:
  N1: S1.Pin_1, S1.Pin_2, R3.Pin_1, Part1.D5_PWM
  N2: S1.Pin_3, S1.Pin_4, Part1.GND, R4.Pin_1
  N3: Part1.5V, S2.Pin_1, S2.Pin_2
  N4: Part1.D12/A11, S2.Pin_3, S2.Pin_4, R4.Pin_0
